# Fritzing sketch currentsource_mod (saved by Fritzing 0.9.2b)
breadboards: 1

parts:
  IC1 = Dual Op-Amp [package=dip08]
  R1 = Resistor [tolerance=±5% resistance=100 package="0402 [SMD]"]
  Q1 = Basic FET N-Channel [package="TO220 [THT]"]
  I_out- = Header 1 [package=1x01_offset]
  I_out+ = Header 1 [package=1x01_offset]
  Rsense = Resistor [tolerance=±5% resistance=0.1 power=2W package="0402 [SMD]"]
  V_pwr+ = Header 1 [package=1x01_offset]
  GND_pwr = Header 1 [package=1x01_offset]
  R2 = Resistor [tolerance=±5% resistance=100k package="0402 [SMD]"]
  C1 = Electrolytic Capacitor [capacitance=1µF package="100 mil [THT, electrolytic]"]
  I_set = Header 1 [package=1x01_offset]
  V_ctl = Header 1 [package=1x01_offset]
  GND_ctrl = Header 1 [package=1x01_offset]
  R3 = Resistor [tolerance=±5% resistance=100k package="0402 [SMD]"]
  Q2 = NPN-Transistor [package="SOT-23 [SMD]"]
  R4 = Resistor [tolerance=±5% resistance=1k package="0402 [SMD]"]
  PWM = Header 1 [package=1x01_offset]
  Rsense1 = Resistor [tolerance=±5% resistance=0.1 power=2W package="0402 [SMD]"]

nets:
  N1: IC1.A_OUT, IC1.A_-IN, R3.Pin_0
  N2: IC1.A_+IN, R2.Pin_1, C1.+
  N3: IC1.A_V-, Rsense.Pin_1, GND_pwr.1, C1.-, GND_ctrl.1, Q2.2, Rsense1.Pin_1
  N4: IC1.B_+IN, R3.Pin_1, Q2.1
  N5: IC1.B_-IN, Q1.source, Rsense.Pin_0
  N6: IC1.B_OUT, R1.Pin_0
  N7: IC1.A_V+, V_ctl.1
  N8: R1.Pin_1, Q1.gate
  N9: Q1.drain, I_out-.1
  N10: I_out+.1, V_pwr+.1
  N11: R2.Pin_0, I_set.1
  N12: Q2.0, R4.Pin_1
  N13: R4.Pin_0, PWM.1, Rsense1.Pin_0
